# Fritzing sketch DrumaticAffect (saved by Fritzing 0.9.10b)

parts:
  Part1 = Arduino Nano (Rev3.0)
  VCC1 = Battery block 9V
  D1 = Diode [package=diode-1n4001]
  D2 = Diode [package=diode-1n4001]
  RE1 = Rotary Encoder [package=THT]
  S1 = SWITCH-MOMENTARY-2 [package=tactile-pth]
  S3 = Toggle Switch [package=THT]
  Grove1 = Grove OLED 128x96
  DS2Y-5-DC5V1 = DS2Y-5-DC5V [part_number=DS2Y-5-DC5V]
  DS2Y-5-DC5V2 = DS2Y-5-DC5V [part_number=DS2Y-5-DC5V]
  S6 = SWITCH-SP3T [package=switch-sp3t-smd]
  U1 = AUDIO-JACK2 [package=audio-jack-3.5mm-smd]
  U2 = AUDIO-JACK2 [package=audio-jack-3.5mm-smd]

nets:
  GND: Part1.GND, VCC1.-, RE1.EncoderPinC, S1.2, Grove1.GND, DS2Y-5-DC5V1.16_-, DS2Y-5-DC5V2.16_-
  N1: Part1.D2, RE1.EncoderPinB
  N2: Part1.D3, RE1.EncoderPinA
  N3: Part1.D4, S1.1
  N4: Part1.D5, DS2Y-5-DC5V1.1_+
  N5: Part1.D6, DS2Y-5-DC5V2.1_+
  N6: Part1.VIN, VCC1.+
  5V: Part1.5V, Grove1.VCC
  N7: Part1.A5, Grove1.SCL
  N8: Part1.A4, Grove1.SDA
  N9: D1.C, D2.C, S6.4
  N10: D2.A, S6.3, U2.RING
  N11: S3.L1, U1.TIP
  N12: S3.COM, DS2Y-5-DC5V2.8_N.O.
  N13: DS2Y-5-DC5V1.8_N.O., U2.SLEEVE
  N14: DS2Y-5-DC5V1.4_COM, S6.1
  N15: DS2Y-5-DC5V2.4_COM, U1.SLEEVE
  N16: S6.2, U2.TIP

notes:
  Goes to FSX3 input
  Goes to pedal switch tap
  3PST manual switch to select verse, chorus, or bridge
  Switch enables auto-start feature
